// Logisim project CPU.circ as structural Verilog: 8 circuits, main circuit main
module main (
  input  ENA,
  input  CLEAR,
  input  LOAD,
  input  ENA_2,
  input  CLEAR_2,
  input  LOAD_2,
  input  ENA_3,
  input  CLEAR_3,
  input  LOAD_3,
  input  E0,
  input  SU,
  input  D1,
  input  D2,
  input  D3,
  input  D4,
  input  D5,
  input  D6,
  input  D7,
  input  D8
);

  wire and_1_out, not_1_out, not_2_out, not_3_out, not_4_out, timer_1_output;
  wire [3:0] octalbustransceiver_3_q;
  wire [7:0] alu_1_result, dreg8bit_1_q, dreg8bit_2_q, dreg8bit_3_q;

  TIMER timer_1 (.Output(timer_1_output));  // open: Select, Pulse, Hlt
  DREG8BIT dreg8bit_1 (.CLEAR(CLEAR), .LOAD(LOAD), .D(alu_1_result), .CLOCK(timer_1_output), .Q(dreg8bit_1_q));
  DREG8BIT dreg8bit_2 (.CLEAR(CLEAR_2), .LOAD(LOAD_2), .D(alu_1_result), .CLOCK(timer_1_output), .Q(dreg8bit_2_q));
  DREG8BIT dreg8bit_3 (.CLEAR(CLEAR_3), .LOAD(LOAD_3), .D(alu_1_result), .CLOCK(timer_1_output), .Q(dreg8bit_3_q));
  LED led_1 (.in(timer_1_output));
  not not_1 (not_1_out, E0);
  LED led_2 (.in(dreg8bit_1_q[7]));
  LED led_3 (.in(dreg8bit_1_q[5]));
  LED led_4 (.in(dreg8bit_1_q[6]));
  LED led_5 (.in(dreg8bit_1_q[4]));
  LED led_6 (.in(dreg8bit_2_q[3]));
  LED led_7 (.in(dreg8bit_2_q[1]));
  LED led_8 (.in(dreg8bit_2_q[0]));
  LED led_9 (.in(dreg8bit_2_q[2]));
  LED led_10 (.in(dreg8bit_3_q[2]));
  LED led_11 (.in(dreg8bit_3_q[0]));
  LED led_12 (.in(dreg8bit_3_q[3]));
  LED led_13 (.in(dreg8bit_3_q[1]));
  ALU alu_1 (.A(dreg8bit_1_q), .B(dreg8bit_2_q), .E0(E0), .SU(SU), .Result(alu_1_result));  // open: Carry
  LED led_14 (.in(dreg8bit_1_q[2]));
  LED led_15 (.in(dreg8bit_1_q[0]));
  LED led_16 (.in(dreg8bit_1_q[3]));
  LED led_17 (.in(dreg8bit_1_q[1]));
  LED led_18 (.in(dreg8bit_2_q[6]));
  LED led_19 (.in(dreg8bit_2_q[4]));
  LED led_20 (.in(dreg8bit_2_q[7]));
  LED led_21 (.in(dreg8bit_2_q[5]));
  LED led_22 (.in(dreg8bit_3_q[7]));
  LED led_23 (.in(dreg8bit_3_q[5]));
  LED led_24 (.in(dreg8bit_3_q[6]));
  LED led_25 (.in(dreg8bit_3_q[4]));
  OCTALBUSTRANSCEIVER octalbustransceiver_1 (.D(dreg8bit_1_q), .ENA(ENA), .Q(alu_1_result));
  OCTALBUSTRANSCEIVER octalbustransceiver_2 (.D(dreg8bit_2_q), .ENA(ENA_2), .Q(alu_1_result));
  OCTALBUSTRANSCEIVER octalbustransceiver_3 (
    .D(dreg8bit_3_q), .ENA(ENA_3), .Q({alu_1_result[7:4], octalbustransceiver_3_q}));
  LED led_26 (.in(alu_1_result[0]));
  not not_2 (not_2_out, ENA);
  not not_3 (not_3_out, ENA_2);
  not not_4 (not_4_out, ENA_3);
  assign alu_1_result[0] = and_1_out ? D1 : 1'bz;  // Controlled_Buffer controlled_buffer_1
  LED led_27 (.in(alu_1_result[1]));
  LED led_28 (.in(alu_1_result[3]));
  LED led_29 (.in(alu_1_result[4]));
  LED led_30 (.in(alu_1_result[2]));
  assign alu_1_result[4] = and_1_out ? D5 : 1'bz;  // Controlled_Buffer controlled_buffer_2
  assign alu_1_result[3] = and_1_out ? D4 : 1'bz;  // Controlled_Buffer controlled_buffer_3
  assign alu_1_result[2] = and_1_out ? D3 : 1'bz;  // Controlled_Buffer controlled_buffer_4
  assign alu_1_result[1] = and_1_out ? D2 : 1'bz;  // Controlled_Buffer controlled_buffer_5
  LED led_31 (.in(alu_1_result[5]));
  LED led_32 (.in(alu_1_result[6]));
  LED led_33 (.in(alu_1_result[7]));
  assign alu_1_result[5] = and_1_out ? D6 : 1'bz;  // Controlled_Buffer controlled_buffer_6
  assign alu_1_result[6] = and_1_out ? D7 : 1'bz;  // Controlled_Buffer controlled_buffer_7
  assign alu_1_result[7] = and_1_out ? D8 : 1'bz;  // Controlled_Buffer controlled_buffer_8
  and and_1 (and_1_out, not_4_out, not_3_out, not_2_out, not_1_out);
endmodule

module TIMER (
  input  Select,
  input  Pulse,
  input  Hlt,
  output Output
);

  wire and_1_out, and_2_out, clock_1_out, not_1_out, not_2_out, or_1_out;

  Clock clock_1 (.out(clock_1_out));
  not not_1 (not_1_out, Select);
  and and_1 (and_1_out, clock_1_out, not_1_out);
  and and_2 (and_2_out, Select, Pulse);
  or or_1 (or_1_out, and_1_out, and_2_out);
  and and_3 (Output, or_1_out, not_2_out);
  not not_2 (not_2_out, Hlt);
endmodule

module DREG8BIT (
  input  CLEAR,
  input  LOAD,
  input  [7:0] D,
  input  CLOCK,
  output [7:0] Q
);

  wire and_1_out, and_2_out, and_3_out, and_4_out, and_5_out, and_6_out, and_7_out, and_8_out, and_9_out,
       and_10_out, and_11_out, and_12_out, and_13_out, and_14_out, and_15_out, and_16_out, d_ff_3_q,
       d_ff_3_qn, d_ff_5_q, d_ff_5_qn, d_ff_9_q, d_ff_9_qn, d_ff_11_q, d_ff_11_qn, not_1_out, not_2_out,
       not_3_out, not_4_out, not_5_out, not_6_out, not_7_out, not_8_out, or_1_out, or_2_out, or_3_out,
       or_4_out, or_5_out, or_6_out, or_7_out, or_8_out, undriven, undriven_2, undriven_3, undriven_4,
       undriven_5, undriven_6, undriven_7, undriven_8, undriven_9, undriven_10, undriven_11, undriven_12,
       undriven_13, undriven_14, undriven_15, undriven_16;

  not not_1 (not_1_out, LOAD);
  not not_2 (not_2_out, LOAD);
  not not_3 (not_3_out, LOAD);
  not not_4 (not_4_out, LOAD);
  not not_5 (not_5_out, LOAD);
  not not_6 (not_6_out, LOAD);
  not not_7 (not_7_out, LOAD);
  not not_8 (not_8_out, LOAD);
  and and_1 (and_1_out, Q[0], not_1_out);
  and and_2 (and_2_out, LOAD, D[0]);
  and and_3 (and_3_out, Q[1], not_2_out);
  and and_4 (and_4_out, LOAD, D[1]);
  and and_5 (and_5_out, Q[2], not_3_out);
  and and_6 (and_6_out, LOAD, D[2]);
  and and_7 (and_7_out, Q[3], not_4_out);
  and and_8 (and_8_out, LOAD, D[3]);
  and and_9 (and_9_out, Q[4], not_5_out);
  and and_10 (and_10_out, LOAD, D[4]);
  and and_11 (and_11_out, Q[5], not_6_out);
  and and_12 (and_12_out, LOAD, D[5]);
  and and_13 (and_13_out, Q[6], not_7_out);
  and and_14 (and_14_out, LOAD, D[6]);
  and and_15 (and_15_out, Q[7], not_8_out);
  and and_16 (and_16_out, LOAD, D[7]);
  D_Flip_Flop d_ff_1 (.D(or_1_out), .clk(CLOCK), .Q(Q[0]), .reset(CLEAR));  // open: Qn, preset
  or or_1 (or_1_out, and_1_out, and_2_out);
  D_Flip_Flop d_ff_2 (.D(or_2_out), .clk(CLOCK), .Q(Q[1]), .reset(CLEAR));  // open: Qn, preset
  or or_2 (or_2_out, and_3_out, and_4_out);
  D_Flip_Flop d_ff_3 (
    .clk(undriven), .D(undriven_2), .Q(d_ff_3_q), .Qn(d_ff_3_qn), .preset(undriven_9), .reset(undriven_13));
  D_Flip_Flop d_ff_4 (
    .clk(undriven), .D(undriven_2), .Q(d_ff_3_q), .Qn(d_ff_3_qn), .preset(undriven_9), .reset(undriven_13));
  or or_3 (or_3_out, and_5_out, and_6_out);
  D_Flip_Flop d_ff_5 (
    .clk(undriven_3), .D(undriven_4), .Q(d_ff_5_q), .Qn(d_ff_5_qn), .preset(undriven_10), .reset(undriven_14));
  D_Flip_Flop d_ff_6 (
    .clk(undriven_3), .D(undriven_4), .Q(d_ff_5_q), .Qn(d_ff_5_qn), .preset(undriven_10), .reset(undriven_14));
  or or_4 (or_4_out, and_7_out, and_8_out);
  D_Flip_Flop d_ff_7 (.D(or_5_out), .clk(CLOCK), .Q(Q[4]), .reset(CLEAR));  // open: Qn, preset
  or or_5 (or_5_out, and_9_out, and_10_out);
  D_Flip_Flop d_ff_8 (.D(or_6_out), .clk(CLOCK), .Q(Q[5]), .reset(CLEAR));  // open: Qn, preset
  or or_6 (or_6_out, and_11_out, and_12_out);
  D_Flip_Flop d_ff_9 (
    .clk(undriven_5), .D(undriven_6), .Q(d_ff_9_q), .Qn(d_ff_9_qn), .preset(undriven_11), .reset(undriven_15));
  D_Flip_Flop d_ff_10 (
    .clk(undriven_5), .D(undriven_6), .Q(d_ff_9_q), .Qn(d_ff_9_qn), .preset(undriven_11), .reset(undriven_15));
  or or_7 (or_7_out, and_13_out, and_14_out);
  D_Flip_Flop d_ff_11 (
    .clk(undriven_7), .D(undriven_8), .Q(d_ff_11_q), .Qn(d_ff_11_qn), .preset(undriven_12),
    .reset(undriven_16));
  D_Flip_Flop d_ff_12 (
    .clk(undriven_7), .D(undriven_8), .Q(d_ff_11_q), .Qn(d_ff_11_qn), .preset(undriven_12),
    .reset(undriven_16));
  or or_8 (or_8_out, and_15_out, and_16_out);
endmodule

module OCTALBUSTRANSCEIVER (
  input  ENA,
  input  [7:0] D,
  output [7:0] Q
);

  assign Q = ENA ? D : 8'bz;  // Controlled_Buffer controlled_buffer_1
endmodule

module ALU (
  input  E0,
  input  [7:0] A,
  input  [7:0] B,
  input  SU,
  output [7:0] Result,
  output Carry
);

  wire [7:0] adder8bit_1_out, inverter_1_output;

  INVERTER inverter_1 (.Enable(SU), .Input(B), .Output(inverter_1_output));
  OCTALBUSTRANSCEIVER octalbustransceiver_1 (.D(adder8bit_1_out), .ENA(E0), .Q(Result));
  ADDER8BIT adder8bit_1 (.A(A), .B(inverter_1_output), .Ci(SU), .Out(adder8bit_1_out), .Carry(Carry));
endmodule

module ADDER8BIT (
  input  [7:0] A,
  input  [7:0] B,
  input  Ci,
  output [7:0] Out,
  output Carry
);

  wire adder1bit_1_co, adder1bit_2_co, adder1bit_3_co, adder1bit_4_co, adder1bit_5_co, adder1bit_6_co,
       adder1bit_7_co;

  ADDER1BIT adder1bit_1 (.Ci(Ci), .A(A[0]), .B(B[0]), .Q(Out[0]), .Co(adder1bit_1_co));
  ADDER1BIT adder1bit_2 (.Ci(adder1bit_1_co), .A(A[1]), .B(B[1]), .Q(Out[1]), .Co(adder1bit_2_co));
  ADDER1BIT adder1bit_3 (.Ci(adder1bit_2_co), .A(A[2]), .B(B[2]), .Q(Out[2]), .Co(adder1bit_3_co));
  ADDER1BIT adder1bit_4 (.Ci(adder1bit_3_co), .A(A[3]), .B(B[3]), .Q(Out[3]), .Co(adder1bit_4_co));
  ADDER1BIT adder1bit_5 (.Ci(adder1bit_4_co), .A(A[4]), .B(B[4]), .Q(Out[4]), .Co(adder1bit_5_co));
  ADDER1BIT adder1bit_6 (.Ci(adder1bit_5_co), .A(A[5]), .B(B[5]), .Q(Out[5]), .Co(adder1bit_6_co));
  ADDER1BIT adder1bit_7 (.Ci(adder1bit_6_co), .A(A[6]), .B(B[6]), .Q(Out[6]), .Co(adder1bit_7_co));
  ADDER1BIT adder1bit_8 (.Ci(adder1bit_7_co), .A(A[7]), .B(B[7]), .Q(Out[7]), .Co(Carry));
endmodule

module ADDER1BIT (
  input  Ci,
  input  A,
  input  B,
  output Q,
  output Co
);

  wire and_1_out, and_2_out, xor_1_out;

  xor xor_1 (xor_1_out, A, B);
  and and_1 (and_1_out, xor_1_out, Ci);
  and and_2 (and_2_out, A, B);
  xor xor_2 (Q, xor_1_out, Ci);
  or or_1 (Co, and_1_out, and_2_out);
endmodule

module INVERTER (
  input  Enable,
  input  [7:0] Input,
  output [7:0] Output
);

  xor xor_1 (Output[0], Input[0], Enable);
  xor xor_2 (Output[1], Input[1], Enable);
  xor xor_3 (Output[3], Input[3], Enable);
  xor xor_4 (Output[2], Input[2], Enable);
  xor xor_5 (Output[5], Input[5], Enable);
  xor xor_6 (Output[4], Input[4], Enable);
  xor xor_7 (Output[7], Input[7], Enable);
  xor xor_8 (Output[6], Input[6], Enable);
endmodule
